// Logisim project ALU Design.circ as structural Verilog: 1 circuit, main circuit main
module main (
  input  [31:0] Value1,
  input  [31:0] Value2,
  input  [2:0] in_3,
  output [31:0] result
);

  wire [31:0] adder_1_out, and_1_out, multiplier_1_out, or_1_out, subtractor_1_out;

  assign and_1_out = Value1 & Value2;  // AND_Gate and_1, 32 bits wide
  assign or_1_out = Value1 | Value2;  // OR_Gate or_1, 32 bits wide
  Adder #(.width(32)) adder_1 (.a(Value1), .b(Value2), .out(adder_1_out));  // open: cin, cout
  Subtractor #(.width(32)) subtractor_1 (.a(Value1), .b(Value2), .out(subtractor_1_out));  // open: bin, bout
  Multiplier #(.width(32)) multiplier_1 (.a(Value1), .b(Value2), .out(multiplier_1_out));  // open: cin, cout
  Multiplexer #(.select(3), .width(32)) multiplexer_1 (
    .in0(and_1_out), .in1(or_1_out), .in2(adder_1_out), .in3(subtractor_1_out), .in4(multiplier_1_out),
    .out(result), .sel(in_3));  // open: in5, in6, in7, en
endmodule
