// Logisim project Control Unit.circ as structural Verilog: 1 circuit, main circuit main
module main (
  input  [31:0] Instruction,
  output RegDST,
  output RegWrite,
  output ALUSrc,
  output jump
);

  wire AddI_out, not_1_out, not_2_out, not_3_out, not_4_out, not_5_out, not_6_out, not_7_out, not_8_out,
       not_9_out, not_10_out, not_11_out, not_12_out, not_13_out, not_14_out, not_15_out, not_16_out,
       not_17_out, not_18_out, not_19_out, not_20_out, not_21_out, not_22_out, not_23_out, not_24_out,
       OrI_out, SubI_out;

  not not_1 (not_1_out, Instruction[26]);
  not not_2 (not_2_out, Instruction[27]);
  not not_3 (not_3_out, Instruction[28]);
  not not_4 (not_4_out, Instruction[30]);
  not not_5 (not_5_out, Instruction[31]);
  not not_6 (not_6_out, Instruction[27]);
  not not_7 (not_7_out, Instruction[28]);
  not not_8 (not_8_out, Instruction[30]);
  not not_9 (not_9_out, Instruction[31]);
  not not_10 (not_10_out, Instruction[26]);
  not not_11 (not_11_out, Instruction[27]);
  not not_12 (not_12_out, Instruction[30]);
  not not_13 (not_13_out, Instruction[31]);
  not not_14 (not_14_out, Instruction[26]);
  not not_15 (not_15_out, Instruction[28]);
  not not_16 (not_16_out, Instruction[29]);
  not not_17 (not_17_out, Instruction[30]);
  not not_18 (not_18_out, Instruction[31]);
  not not_19 (not_19_out, Instruction[26]);
  not not_20 (not_20_out, Instruction[27]);
  not not_21 (not_21_out, Instruction[28]);
  not not_22 (not_22_out, Instruction[29]);
  not not_23 (not_23_out, Instruction[30]);
  not not_24 (not_24_out, Instruction[31]);
  and R_Type (RegDST, not_19_out, not_20_out, not_21_out, not_22_out, not_23_out, not_24_out);
  and AddI (AddI_out, not_1_out, not_2_out, not_3_out, Instruction[29], not_4_out, not_5_out);
  and SubI (SubI_out, Instruction[26], not_6_out, not_7_out, Instruction[29], not_8_out, not_9_out);
  and OrI (OrI_out, not_10_out, not_11_out, Instruction[28], Instruction[29], not_12_out, not_13_out);
  and J (jump, not_14_out, Instruction[27], not_15_out, not_16_out, not_17_out, not_18_out);
  or or_1 (RegWrite, RegDST, AddI_out, SubI_out, OrI_out);
  or or_2 (ALUSrc, AddI_out, SubI_out, OrI_out);

  // Notes on the sheet:
  //   Opcode
endmodule
